// Logisim project ALU.circ as structural Verilog
module Mult_Signed (
  input  [31:0] A,
  input  [31:0] B,
  output [31:0] Hi,
  output [31:0] Lo
);

  wire [30:0] Carry, Carry_t, Carry_t_t, Carry_t_t_t, multiplier_1_out, multiplier_2_out, multiplier_3_out,
       multiplier_4_out, negator_1_out, negator_2_out, negator_3_out, negator_5_out;
  wire [31:0] negator_4_out, negator_6_out, negator_7_out, negator_8_out;

  // Probe on A
  // Probe on B
  Multiplier #(.width(31)) multiplier_1 (.a(A[30:0]), .b(B[30:0]), .out(multiplier_1_out), .cout(Carry));  // open: cin
  Negator #(.width(31)) negator_1 (.in(B[30:0]), .out(negator_1_out));
  Negator #(.width(31)) negator_2 (.in(A[30:0]), .out(negator_2_out));
  Negator #(.width(31)) negator_3 (.in(B[30:0]), .out(negator_3_out));
  Negator #(.width(32)) negator_4 (.in({1'b0, Carry_t_t}), .out(negator_4_out));
  Negator #(.width(31)) negator_5 (.in(A[30:0]), .out(negator_5_out));
  Multiplier #(.width(31)) multiplier_2 (
    .a(negator_5_out), .b(B[30:0]), .out(multiplier_2_out), .cout(Carry_t_t));  // open: cin
  Multiplier #(.width(31)) multiplier_3 (
    .a(A[30:0]), .b(negator_1_out), .out(multiplier_3_out), .cout(Carry_t));  // open: cin
  Negator #(.width(32)) negator_6 (.in({1'b0, Carry_t}), .out(negator_6_out));
  Multiplier #(.width(31)) multiplier_4 (
    .a(negator_2_out), .b(negator_3_out), .out(multiplier_4_out), .cout(Carry_t_t_t));  // open: cin
  Negator #(.width(32)) negator_7 (.in({1'b0, multiplier_2_out}), .out(negator_7_out));
  Negator #(.width(32)) negator_8 (.in({1'b0, multiplier_3_out}), .out(negator_8_out));
  Multiplexer #(.select(2), .width(32), .enable("false")) multiplexer_1 (
    .in0({1'b0, multiplier_1_out}), .in1(negator_7_out), .in2(negator_8_out), .in3({1'b0, multiplier_4_out}),
    .out(Hi), .sel({B[31], A[31]}));
  // Probe on Lo
  Multiplexer #(.select(2), .width(32), .enable("false")) multiplexer_2 (
    .in0({1'b0, Carry}), .in1(negator_4_out), .in2(negator_6_out), .in3({1'b0, Carry_t_t_t}), .out(Lo),
    .sel({B[31], A[31]}));
  // Probe on Hi

  // Other names for the same wires on the sheet: A_signed = A[31]; B_signed = B[31]; A_t[30:0] = A[30:0];
  //   B_t[30:0] = B[30:0]

  // Notes on the sheet:
  //   ++
  //   -+
  //   +-
  //   --
endmodule

module Div_Signed (
  input  [31:0] A,
  input  [31:0] B,
  output [31:0] Hi,
  output [31:0] Lo
);

  wire [30:0] Carry, Carry_t, Carry_t_t, Carry_t_t_t, divider_1_out, divider_2_out, divider_3_out,
       divider_4_out, negator_1_out, negator_2_out, negator_3_out, negator_5_out;
  wire [31:0] negator_4_out, negator_6_out, negator_7_out, negator_8_out;

  // Probe on A
  // Probe on B
  Divider #(.width(31)) divider_1 (.a(A[30:0]), .b(B[30:0]), .out(divider_1_out), .rem(Carry));  // open: upper
  Negator #(.width(31)) negator_1 (.in(B[30:0]), .out(negator_1_out));
  Negator #(.width(31)) negator_2 (.in(A[30:0]), .out(negator_2_out));
  Negator #(.width(31)) negator_3 (.in(B[30:0]), .out(negator_3_out));
  Negator #(.width(32)) negator_4 (.in({1'b0, Carry_t_t}), .out(negator_4_out));
  Negator #(.width(31)) negator_5 (.in(A[30:0]), .out(negator_5_out));
  Divider #(.width(31)) divider_2 (
    .a(negator_5_out), .b(B[30:0]), .out(divider_2_out), .rem(Carry_t_t));  // open: upper
  Divider #(.width(31)) divider_3 (.a(A[30:0]), .b(negator_1_out), .out(divider_3_out), .rem(Carry_t));  // open: upper
  Negator #(.width(32)) negator_6 (.in({1'b0, Carry_t}), .out(negator_6_out));
  Divider #(.width(31)) divider_4 (
    .a(negator_2_out), .b(negator_3_out), .out(divider_4_out), .rem(Carry_t_t_t));  // open: upper
  Negator #(.width(32)) negator_7 (.in({1'b0, divider_2_out}), .out(negator_7_out));
  Negator #(.width(32)) negator_8 (.in({1'b0, divider_3_out}), .out(negator_8_out));
  Multiplexer #(.select(2), .width(32), .enable("false")) multiplexer_1 (
    .in0({1'b0, divider_1_out}), .in1(negator_7_out), .in2(negator_8_out), .in3({1'b0, divider_4_out}),
    .out(Hi), .sel({B[31], A[31]}));
  // Probe on Lo
  Multiplexer #(.select(2), .width(32), .enable("false")) multiplexer_2 (
    .in0({1'b0, Carry}), .in1(negator_4_out), .in2(negator_6_out), .in3({1'b0, Carry_t_t_t}), .out(Lo),
    .sel({B[31], A[31]}));
  // Probe on Hi

  // Other names for the same wires on the sheet: A_signed = A[31]; B_signed = B[31]; A_t[30:0] = A[30:0];
  //   B_t[30:0] = B[30:0]

  // Notes on the sheet:
  //   -+
  //   +-
  //   --
endmodule

module ALU (
  input  [31:0] A,
  input  [3:0] in_2,
  input  [31:0] B,
  output [31:0] Hi,
  output [31:0] Lo
);

  wire BorrowRest, comparator_1_gt, comparator_2_lt, CoutAdd;
  wire [31:0] Add, \and , Div_Signed, Divu, Lo_Div_Signed, Lo_Divu, Lo_Mult_Signed, Lo_Mulu, Mult_Signed,
       Mulu, \nor , \or , Subs, tunnel, tunnel_t, \xor ;

  // Probe on A
  // Probe on B
  Multiplier #(.width(32)) multiplier_1 (.a(A), .b(B), .out(Mulu), .cout(Lo_Mulu));  // open: cin
  Divider #(.width(32)) divider_1 (.a(A), .b(B), .out(Divu), .rem(Lo_Divu));  // open: upper
  assign \and  = A & B;  // AND_Gate and_1, 32 bits wide
  assign \or  = A | B;  // OR_Gate or_1, 32 bits wide
  assign \nor  = ~(A | B);  // NOR_Gate nor_1, 32 bits wide
  Comparator #(.width(32)) comparator_1 (.a(A), .b(B), .gt(comparator_1_gt));  // open: eq, lt
  Comparator #(.width(32)) comparator_2 (.a(A), .b(B), .lt(comparator_2_lt));  // open: gt, eq
  Mult_Signed mult_signed_1 (.A(A), .B(B), .Hi(Mult_Signed), .Lo(Lo_Mult_Signed));
  Div_Signed div_signed_1 (.A(A), .B(B), .Hi(Div_Signed), .Lo(Lo_Div_Signed));
  assign \xor  = A ^ B;  // XOR_Gate xor_1, 32 bits wide
  Multiplexer #(.width(32), .enable("false")) multiplexer_1 (
    .in0({32{1'b0}}), .in1(32'h1), .out(tunnel_t), .sel(comparator_1_gt));
  Multiplexer #(.width(32), .enable("false")) multiplexer_2 (
    .in0({32{1'b0}}), .in1(32'h1), .out(tunnel), .sel(comparator_2_lt));
  Adder #(.width(32)) adder_1 (.a(A), .b(B), .out(Add), .cout(CoutAdd));  // open: cin
  Subtractor #(.width(32)) subtractor_1 (.a(A), .b(B), .out(Subs), .bout(BorrowRest));  // open: bin
  // Probe on Hi
  Multiplexer #(.select(4), .width(32), .enable("false")) multiplexer_3 (
    .in0(Add), .in1(Subs), .in2(Mulu), .in3(Mult_Signed), .in4(Divu), .in5(Div_Signed), .in6(tunnel_t),
    .in7(tunnel), .in8(\and ), .in9(\or ), .in10(\nor ), .in11(\xor ), .out(Hi), .sel(in_2));  // open: in12, in13, in14, in15
  // Probe on Lo
  Multiplexer #(.select(2), .width(32), .enable("false")) multiplexer_4 (
    .in0(Lo_Mulu), .in1(Lo_Mult_Signed), .in2(Lo_Divu), .in3(Lo_Div_Signed), .out(Lo),
    .sel({in_2[2], in_2[0]}));

  // Other names for the same wires on the sheet: Selector[3:0] = in_2

  // Notes on the sheet:
  //   LOGICAS
endmodule
