// Logisim project CACHE-Unit.circ as structural Verilog: 2 circuits, main circuit Contador de Ciclos
module Contador_de_Ciclos (
  input  [3:0] Read_Time,
  input  [3:0] Write_Time,
  input  Reloj,
  input  R_W,
  input  in_5,
  input  in_6,
  output WAIT
);

  wire [3:0] counter_1_q, RT__WT;

  Multiplexer #(.width(4), .enable("false")) multiplexer_1 (.in0(Read_Time), .in1(Write_Time), .out(RT__WT), .sel(R_W));
  Counter #(.width(4), .max('hf)) counter_1 (
    .count(in_5), .Q(counter_1_q), .clk(Reloj), .clr(in_6));  // open: load, D, carry
  Comparator #(.width(4)) comparator_1 (.a(counter_1_q), .b(RT__WT), .eq(WAIT));  // open: gt, lt

  // Other names for the same wires on the sheet: CLK = Reloj; CS = in_5; RST = in_6

  // Notes on the sheet:
  //   Entradas de Tiempo
  //   Contador de Ciclos del Reloj
endmodule

module CACHE_UNIT (
  input  in_1,
  input  RST,
  input  in_3,
  input  rw,
  input  [3:0] in_5,
  input  [3:0] in_6,
  input  in_7,
  input  in_8,
  input  [31:0] ADRESS,
  input  LOADADRESS,
  input  [31:0] in_11,
  input  in_12,
  input  [31:0] in_13,
  input  [31:0] in_14,
  input  [31:0] in_15,
  output FINISH,
  output CST,
  output [31:0] out_18,
  output [15:0] RAMADRESS,
  output [31:0] out_20,
  output RW_RAM,
  output [31:0] out_22,
  output [31:0] out_23,
  output [31:0] out_24,
  output [31:0] out_25
);

  wire and_1_out, C1, C2, cache_1_finishcacheline, CLEAN, CS1, CS2, CS3, CS4, CS5, CS6, D, D1, D2, D3,
       d_ff_1_q, d_ff_6_q, d_ff_8_q, demultiplexer_1_out0, demultiplexer_1_out1, demultiplexer_2_out0,
       demultiplexer_2_out1, demultiplexer_3_out0, demultiplexer_4_out0, demultiplexer_5_out0,
       demultiplexer_5_out1, demultiplexer_6_out0, demultiplexer_6_out1, demultiplexer_7_out0,
       demultiplexer_8_out0, demultiplexer_9_out0, demultiplexer_10_out0, demultiplexer_11_out0,
       demultiplexer_12_out0, DIRTY, F1, F2, F3, HINT, L3, L4, LINEA, not_1_out, or_1_out, or_2_out,
       or_3_out, or_4_out, or_5_out, or_10_out, or_12_out, RA, RW_t, VALIDO, WAIT;

  or or_1 (or_1_out, CS5, CS2);
  and and_1 (and_1_out, ~in_7, ~RST);  // AND_Gate
  Demultiplexer demultiplexer_1 (
    .out0(demultiplexer_1_out0), .out1(demultiplexer_1_out1), .in(d_ff_1_q), .sel(in_7));  // open: en
  D_Flip_Flop d_ff_1 (
    .clk(in_3), .D(demultiplexer_1_out0), .Q(d_ff_1_q), .preset(and_1_out), .reset(RST));  // open: Qn, en
  not not_1 (not_1_out, CST);
  Contador_de_Ciclos contador_de_ciclos_1 (
    .Read_Time(in_5), .Write_Time(in_6), .Reloj(in_3), .R_W(or_1_out), .in_5(CST), .in_6(not_1_out),
    .WAIT(WAIT));
  CACHE cache_1 (
    .Adress(ADRESS), .in_4(in_11), .in_5(in_13), .in_6(in_14), .in_7(in_15), .Rst(RST), .OUT(out_22),
    .O1(out_18), .O2(out_20), .O2_2(out_23), .O4(out_24), .HINT(HINT), .DIRTY_2(DIRTY), .CLK(in_3),
    .DIRTY(D), .valid(VALIDO), .RAMADRESS(RAMADRESS), .CLEAN(CLEAN),
    .finishcacheline(cache_1_finishcacheline), .LoadAdress(LOADADRESS), .RW(RW_t), .LINEA(LINEA),
    .in_9(in_12), .data(out_25), .RST_OUT(in_8), .in_11(RA));
  Demultiplexer demultiplexer_2 (
    .out0(demultiplexer_2_out0), .out1(demultiplexer_2_out1), .in(demultiplexer_1_out1), .sel(rw));  // open: en
  Demultiplexer demultiplexer_3 (
    .out0(demultiplexer_3_out0), .out1(D1), .in(demultiplexer_2_out1), .sel(HINT));  // open: en
  Demultiplexer demultiplexer_4 (
    .out0(demultiplexer_4_out0), .out1(F1), .in(demultiplexer_2_out0), .sel(HINT));  // open: en
  Demultiplexer demultiplexer_5 (
    .out0(demultiplexer_5_out0), .out1(demultiplexer_5_out1), .in(demultiplexer_3_out0), .sel(DIRTY));  // open: en
  or or_2 (or_2_out, demultiplexer_7_out0, demultiplexer_5_out0);
  Demultiplexer demultiplexer_6 (
    .out0(demultiplexer_6_out0), .out1(demultiplexer_6_out1), .in(demultiplexer_4_out0), .sel(DIRTY));  // open: en
  D_Flip_Flop d_ff_2 (.clk(in_3), .D(or_2_out), .Q(CS4), .en(in_1), .reset(RST));  // open: Qn, preset
  or or_3 (or_3_out, demultiplexer_8_out0, demultiplexer_5_out1);
  or or_4 (or_4_out, demultiplexer_10_out0, demultiplexer_6_out0);
  or or_5 (or_5_out, demultiplexer_6_out1, demultiplexer_9_out0);
  Demultiplexer #(.enable("false")) demultiplexer_7 (.out0(demultiplexer_7_out0), .out1(L3), .in(CS4), .sel(WAIT));
  D_Flip_Flop d_ff_3 (.clk(in_3), .D(or_3_out), .Q(CS5), .en(in_1), .reset(RST));  // open: Qn, preset
  or or_6 (CLEAN, C1, C2);
  D_Flip_Flop d_ff_4 (.clk(in_3), .D(or_5_out), .Q(CS2), .en(in_1), .reset(RST));  // open: Qn, preset
  Demultiplexer demultiplexer_8 (.out0(demultiplexer_8_out0), .out1(C2), .in(CS5), .sel(WAIT));  // open: en
  or or_7 (LINEA, F2, F3, L3, L4);
  or or_8 (RA, CS2, CS5);
  D_Flip_Flop d_ff_5 (.clk(in_3), .D(or_4_out), .Q(CS1), .en(in_1), .reset(RST));  // open: Qn, preset
  Demultiplexer demultiplexer_9 (.out0(demultiplexer_9_out0), .out1(C1), .in(CS2), .sel(WAIT));  // open: en
  D_Flip_Flop d_ff_6 (.clk(in_3), .D(C2), .Q(d_ff_6_q), .en(in_1), .reset(RST));  // open: Qn, preset
  or or_9 (D, D1, D2, D3);
  Demultiplexer demultiplexer_10 (.out0(demultiplexer_10_out0), .out1(F2), .in(CS1), .sel(WAIT));  // open: en
  D_Flip_Flop d_ff_7 (.clk(in_3), .D(L3), .Q(D3), .en(in_1), .reset(RST));  // open: Qn, preset
  or or_10 (or_10_out, demultiplexer_11_out0, d_ff_6_q);
  or or_11 (RW_t, D1, L4, D2, L3, D3, F3, F2);
  D_Flip_Flop d_ff_8 (.clk(in_3), .D(C1), .Q(d_ff_8_q), .en(in_1), .reset(RST));  // open: Qn, preset
  D_Flip_Flop d_ff_9 (.clk(in_3), .D(or_10_out), .Q(CS6), .en(in_1), .reset(RST));  // open: Qn, preset
  Demultiplexer demultiplexer_11 (.out0(demultiplexer_11_out0), .out1(L4), .in(CS6), .sel(WAIT));  // open: en
  or or_12 (or_12_out, demultiplexer_12_out0, d_ff_8_q);
  D_Flip_Flop d_ff_10 (.clk(in_3), .D(L4), .Q(D2), .reset(RST));  // open: Qn, preset, en
  D_Flip_Flop d_ff_11 (.clk(in_3), .D(or_12_out), .Q(CS3), .en(in_1), .reset(RST));  // open: Qn, preset
  or or_13 (RW_RAM, CS2, CS5);
  Demultiplexer demultiplexer_12 (.out0(demultiplexer_12_out0), .out1(F3), .in(CS3), .sel(WAIT));  // open: en
  or or_14 (CST, CS1, CS2, CS3, CS4, CS5, CS6);
  or or_15 (VALIDO, F1, F2, F3, D1, D2, D3);
  D_Flip_Flop END (.clk(in_3), .D(VALIDO), .Q(FINISH), .en(in_1), .reset(RST));  // open: Qn, preset

  // Other names for the same wires on the sheet: CLK = in_3; CS = CST; cs_t = in_7; EN = in_1; RO = in_8; F4 = D1;
  //   RW1 = D1; RW2 = L4; F5 = D2; RW3 = D2; RW4 = L3; F6 = D3; RW5 = D3; L2 = F3; RW6 = F3; L1 = F2; RW7 = F2;
  //   RAMADRESS2 = CS5; RRW2 = CS5; t1 = CS5; RAMADRESS1 = CS2; RRW1 = CS2; t2 = CS2

  // Notes on the sheet:
  //   LEER
  //   HINT
  //   MISS
  //   ESCRIBE ||RESCRIBE DEPENDIENDO  DEL DIRTY 
  //   LEER
  //   ESCRIBE  LA INFO ANTIGUA EN  LA RAM 
  //   ESCRIBIR LA LINEA QUE NO ESTA 
  //   LECTURA DE LA INFO DE LA RAM
  //   CACHE OPERATION
  //   LEER
  //   para reiniciar contador 
  //   ESPERAR CICLO DE CARGA
  //   LEER DE LA RAM LA INFO 
  //   RAM OPERATION
  //   ESPERAR CLOCK  PARA CORRECTO GUARDAADO 
endmodule
