// Logisim project CACHE.circ as structural Verilog
module CACHE (
  input  LoadAdress,
  input  [31:0] Adress,
  input  CLK,
  input  [31:0] in_4,
  input  [31:0] in_5,
  input  [31:0] in_6,
  input  [31:0] in_7,
  input  Rst,
  input  DIRTY,
  input  RW,
  input  valid,
  input  CLEAN,
  input  LINEA,
  output [31:0] OUT,
  output [31:0] O1,
  output [31:0] O2,
  output [31:0] O2_2,
  output [31:0] O4,
  output HINT,
  output DIRTY_2,
  output [15:0] RAMADRESS,
  output finishcacheline
);

  wire C1, C2, C3, C4, comparator_1_eq, demultiplexer_1_out0, demultiplexer_1_out1, demultiplexer_3_out0,
       demultiplexer_3_out1, demultiplexer_3_out2, demultiplexer_3_out3, Dirty1, Dirty2, Dirty3, Dirty4, EN1,
       EN2, EN3, EN4, EN5, EN6, EN7, EN8, EN9, EN10, EN11, EN12, EN13, EN14, EN15, EN16, L1, L2, L3, L4,
       multiplexer_2_out, or_1_out, or_2_out, or_3_out, or_4_out, or_5_out, or_6_out, or_7_out, or_8_out,
       or_9_out, or_10_out, or_11_out, or_12_out, or_13_out, or_14_out, or_15_out, or_16_out, or_17_out,
       or_18_out, or_19_out, or_20_out, V1, V2, V3, V4;
  wire [11:0] multiplexer_1_out, T1, T2, T3, T4;
  wire [31:0] Out1, Out2, Out3, Out4, Out5, Out6, Out7, Out8, Out9, Out10, Out11, Out12, Out13, Out14, Out15,
       Out16;
  wire [31:16] register_1_q;

  Register #(.width(32)) register_1 (
    .D(Adress), .en(LoadAdress), .Q({register_1_q, RAMADRESS}), .clk(CLK));  // open: clr
  Multiplexer #(.select(2), .width(12), .enable("false")) multiplexer_1 (
    .in0(T1), .in1(T2), .in2(T3), .in3(T4), .out(multiplexer_1_out), .sel(RAMADRESS[3:2]));
  Multiplexer #(.select(2), .enable("false")) multiplexer_2 (
    .in0(V1), .in1(V2), .in2(V3), .in3(V4), .out(multiplexer_2_out), .sel(RAMADRESS[3:2]));
  Demultiplexer demultiplexer_1 (
    .out0(demultiplexer_1_out0), .out1(demultiplexer_1_out1), .in(RW), .sel(LINEA));  // open: en
  Comparator #(.width(12)) comparator_1 (
    .a(multiplexer_1_out), .b(RAMADRESS[15:4]), .eq(comparator_1_eq));  // open: gt, lt
  Demultiplexer #(.select(2)) demultiplexer_2 (
    .out0(L1), .out1(L2), .out2(L3), .out3(L4), .in(demultiplexer_1_out1), .sel(RAMADRESS[3:2]));  // open: en
  and and_1 (HINT, comparator_1_eq, multiplexer_2_out);
  Demultiplexer #(.select(2)) demultiplexer_3 (
    .out0(demultiplexer_3_out0), .out1(demultiplexer_3_out1), .out2(demultiplexer_3_out2),
    .out3(demultiplexer_3_out3), .in(demultiplexer_1_out0), .sel(RAMADRESS[1:0]));  // open: en
  Register #(.width(12)) register_2 (.D(RAMADRESS[15:4]), .en(L1), .Q(T1), .clk(CLK), .clr(Rst));
  Register #(.width(12)) register_3 (.D(RAMADRESS[15:4]), .en(L2), .Q(T2), .clk(CLK), .clr(Rst));
  Register #(.width(12)) register_4 (.D(RAMADRESS[15:4]), .en(L3), .Q(T3), .clk(CLK), .clr(Rst));
  Register #(.width(12)) register_5 (.D(RAMADRESS[15:4]), .en(L4), .Q(T4), .clk(CLK), .clr(Rst));
  Demultiplexer #(.select(2)) demultiplexer_4 (
    .out0(EN1), .out1(EN5), .out2(EN9), .out3(EN13), .in(demultiplexer_3_out0), .sel(RAMADRESS[3:2]));  // open: en
  Demultiplexer #(.select(2)) demultiplexer_5 (
    .out0(EN2), .out1(EN6), .out2(EN10), .out3(EN14), .in(demultiplexer_3_out1), .sel(RAMADRESS[3:2]));  // open: en
  Demultiplexer #(.select(2)) demultiplexer_6 (
    .out0(EN3), .out1(EN7), .out2(EN11), .out3(EN15), .in(demultiplexer_3_out2), .sel(RAMADRESS[3:2]));  // open: en
  Demultiplexer #(.select(2)) demultiplexer_7 (
    .out0(EN4), .out1(EN8), .out2(EN12), .out3(EN16), .in(demultiplexer_3_out3), .sel(RAMADRESS[3:2]));  // open: en
  or or_1 (or_1_out, L1, EN1);
  or or_2 (or_2_out, L2, EN5);
  or or_3 (or_3_out, L3, EN9);
  or or_4 (or_4_out, L4, EN13);
  Register #(.width(32)) register_6 (.D(in_4), .en(or_1_out), .Q(Out1), .clk(CLK), .clr(Rst));
  Register #(.width(32)) register_7 (.D(in_4), .en(or_2_out), .Q(Out5), .clk(CLK), .clr(Rst));
  Register #(.width(32)) register_8 (.D(in_4), .en(or_3_out), .Q(Out9), .clk(CLK), .clr(Rst));
  Register #(.width(32)) register_9 (.D(in_4), .en(or_4_out), .Q(Out13), .clk(CLK), .clr(Rst));
  or or_5 (or_5_out, L1, EN2);
  or or_6 (or_6_out, L2, EN6);
  or or_7 (or_7_out, L3, EN10);
  or or_8 (or_8_out, L4, EN14);
  Register #(.width(32)) register_10 (.D(in_5), .en(or_5_out), .Q(Out2), .clk(CLK), .clr(Rst));
  Register #(.width(32)) register_11 (.D(in_5), .en(or_6_out), .Q(Out6), .clk(CLK), .clr(Rst));
  Register #(.width(32)) register_12 (.D(in_5), .en(or_7_out), .Q(Out10), .clk(CLK), .clr(Rst));
  Register #(.width(32)) register_13 (.D(in_5), .en(or_8_out), .Q(Out14), .clk(CLK), .clr(Rst));
  Multiplexer #(.select(2), .enable("false")) multiplexer_3 (
    .in0(Dirty1), .in1(Dirty2), .in2(Dirty3), .in3(Dirty4), .out(DIRTY_2), .sel(RAMADRESS[3:2]));
  Multiplexer #(.select(2), .width(32), .enable("false")) multiplexer_4 (
    .in0(Out1), .in1(Out5), .in2(Out9), .in3(Out13), .out(O1), .sel(RAMADRESS[3:2]));
  Multiplexer #(.select(2), .width(32), .enable("false")) multiplexer_5 (
    .in0(Out2), .in1(Out6), .in2(Out10), .in3(Out14), .out(O2), .sel(RAMADRESS[3:2]));
  Multiplexer #(.select(2), .width(32), .enable("false")) multiplexer_6 (
    .in0(Out3), .in1(Out7), .in2(Out11), .in3(Out15), .out(O2_2), .sel(RAMADRESS[3:2]));
  Multiplexer #(.select(2), .width(32), .enable("false")) multiplexer_7 (
    .in0(Out4), .in1(Out8), .in2(Out12), .in3(Out16), .out(O4), .sel(RAMADRESS[3:2]));
  Multiplexer #(.select(2), .width(32), .enable("false")) multiplexer_8 (
    .in0(O1), .in1(O2), .in2(O2_2), .in3(O4), .out(OUT), .sel(RAMADRESS[1:0]));
  or or_9 (or_9_out, L1, EN3);
  or or_10 (or_10_out, L2, EN7);
  or or_11 (or_11_out, L3, EN11);
  or or_12 (or_12_out, L4, EN15);
  Register #(.width(32)) register_14 (.D(in_6), .en(or_9_out), .Q(Out3), .clk(CLK), .clr(Rst));
  Register #(.width(32)) register_15 (.D(in_6), .en(or_10_out), .Q(Out7), .clk(CLK), .clr(Rst));
  Register #(.width(32)) register_16 (.D(in_6), .en(or_11_out), .Q(Out11), .clk(CLK), .clr(Rst));
  Register #(.width(32)) register_17 (.D(in_6), .en(or_12_out), .Q(Out15), .clk(CLK), .clr(Rst));
  or or_13 (or_13_out, L1, EN4);
  or or_14 (or_14_out, L2, EN8);
  or or_15 (or_15_out, L3, EN12);
  or or_16 (or_16_out, L4, EN16);
  and and_2 (finishcacheline, RAMADRESS[0], RAMADRESS[1]);
  Demultiplexer #(.select(2)) demultiplexer_8 (
    .out0(C1), .out1(C2), .out2(C3), .out3(C4), .in(CLEAN), .sel(RAMADRESS[3:2]));  // open: en
  Register #(.width(32)) register_18 (.D(in_7), .en(or_13_out), .Q(Out4), .clk(CLK), .clr(Rst));
  Register #(.width(32)) register_19 (.D(in_7), .en(or_14_out), .Q(Out8), .clk(CLK), .clr(Rst));
  Register #(.width(32)) register_20 (.D(in_7), .en(or_15_out), .Q(Out12), .clk(CLK), .clr(Rst));
  Register #(.width(32)) register_21 (.D(in_7), .en(or_16_out), .Q(Out16), .clk(CLK), .clr(Rst));
  D_Flip_Flop u_VALID (.clk(CLK), .D(valid), .Q(V1), .en(L1), .reset(Rst));  // open: Qn, preset
  D_Flip_Flop VALID_2 (.clk(CLK), .D(valid), .Q(V2), .en(L2), .reset(Rst));  // open: Qn, preset
  D_Flip_Flop VALID_3 (.clk(CLK), .D(valid), .Q(V3), .en(L3), .reset(Rst));  // open: Qn, preset
  D_Flip_Flop VALID_4 (.clk(CLK), .D(valid), .Q(V4), .en(L4), .reset(Rst));  // open: Qn, preset
  D_Flip_Flop u_Dirty (.clk(CLK), .D(DIRTY), .Q(Dirty1), .en(L1), .reset(or_17_out));  // open: Qn, preset
  or or_17 (or_17_out, Rst, C1);
  D_Flip_Flop u_Dirty_2 (.clk(CLK), .D(DIRTY), .Q(Dirty2), .en(L2), .reset(or_18_out));  // open: Qn, preset
  or or_18 (or_18_out, Rst, C2);
  D_Flip_Flop Dirty_3 (.clk(CLK), .D(DIRTY), .Q(Dirty3), .en(L3), .reset(or_19_out));  // open: Qn, preset
  or or_19 (or_19_out, Rst, C3);
  D_Flip_Flop Dirty_4 (.clk(CLK), .D(DIRTY), .Q(Dirty4), .en(L4), .reset(or_20_out));  // open: Qn, preset
  or or_20 (or_20_out, Rst, C4);

  // Other names for the same wires on the sheet: OFFSET[1:0] = RAMADRESS[1:0]; RAM_ADRESS[15:0] = RAMADRESS;
  //   INDEX[1:0] = RAMADRESS[3:2]; TAG[11:0] = RAMADRESS[15:4]; D1[31:0] = in_4; D2[31:0] = in_5; D3[31:0] = in_6;
  //   D4[31:0] = in_7; DIRTY_t = DIRTY_2; O3[31:0] = O2_2

  // Notes on the sheet:
  //   Adress: pull=down
  //   in_4: pull=down
  //   O2: pull=down
  //   OUT: pull=down
  //   O2_2: pull=down
  //   in_6: pull=down
  //   in_5: pull=down
  //   RAMADRESS: pull=down
  //   O4: pull=down
  //   O1: pull=down
  //   Cargar Linea Correcta
  //   ultimo registro de la linea
  //   Cargar Solo en e registro de la direccion
endmodule
