// Logisim project Control Unit.circ as structural Verilog
module Contador_de_Ciclos (
  input  [3:0] Read_Time,
  input  [3:0] Write_Time,
  input  Reloj,
  input  R_W,
  input  Reset,
  output Leido,
  output Escrito
);

  wire comparator_1_eq;
  wire [3:0] multiplexer_1_out, Registro_Contador_q, Time;

  Counter #(.width(4), .max('hf)) Registro_Contador (
    .Q(Registro_Contador_q), .clk(Reloj), .clr(Reset));  // open: load, D, count, carry
  Multiplexer #(.width(4), .enable("false")) multiplexer_1 (
    .in0(Read_Time), .in1(Write_Time), .out(multiplexer_1_out), .sel(R_W));
  Comparator #(.width(4), .mode("unsigned")) comparator_1 (
    .a(Registro_Contador_q), .b(Time), .eq(comparator_1_eq));  // open: gt, lt
  Demultiplexer #(.enable("false")) demultiplexer_1 (.out0(Leido), .out1(Escrito), .in(comparator_1_eq), .sel(R_W));
  Adder #(.width(4)) adder_1 (.a(multiplexer_1_out), .b(4'b0001), .out(Time));  // open: cin, cout

  // Other names for the same wires on the sheet: CLK = Reloj

  // Notes on the sheet:
  //   Entradas de Tiempo
  //   Contador de Ciclos del Reloj
endmodule

// esperar actualizacion PC
module Control_Unit (
  input  Reloj,
  input  Reset,
  input  [3:0] operacion,
  input  Wait,
  input  in_5,
  output \end ,
  output Load_Register_File,
  output Escribir_RAM,
  output RAM_Control,
  output KBD_ENABLE,
  output Load_Program_Counter,
  output LoadMemory,
  output LOADSP,
  output TTY_ENABLE,
  output out_15,
  output out_16
);

  wire ALU_Tip_R_and_Tip_I, Camb_Instr, cambio_de_linea_2_q, cambio_de_linea_q, d_ff_1_q, d_ff_3_q, d_ff_4_q,
       d_ff_5_q, d_ff_6_q, d_ff_7_q, d_ff_12_q, d_ff_13_q, d_ff_15_q, d_ff_16_q, d_ff_17_q,
       demultiplexer_1_out0, demultiplexer_1_out1, demultiplexer_2_out0, demultiplexer_4_out0,
       demultiplexer_5_out0, demultiplexer_6_out0, demultiplexer_6_out1, demultiplexer_7_out0,
       demultiplexer_7_out1, demultiplexer_8_out0, demultiplexer_8_out1, EN_RND, GUARDAR_DATO_2_q,
       GUARDAR_DATO_q, Halt, Jmp_nop_Jr, KBD, LeerNuevaLinea, LI, LI1, LM1, LM2, LM3, LM4, LM5, LSP1, LSP2,
       M1, M2, M3, M4, M5, Mov_Operation, not_1_out, or_1_out, or_5_out, or_6_out, or_7_out, or_8_out,
       or_9_out, or_14_out, or_15_out, or_16_out, R_W_RF2;

  D_Flip_Flop d_ff_1 (.clk(Reloj), .D(demultiplexer_1_out0), .Q(d_ff_1_q), .preset(Reset));  // open: Qn, en, reset
  Demultiplexer #(.enable("false")) demultiplexer_1 (
    .out0(demultiplexer_1_out0), .out1(demultiplexer_1_out1), .in(d_ff_1_q), .sel(not_1_out));
  not not_1 (not_1_out, Reset);
  D_Flip_Flop Insruction_Read (.clk(Reloj), .D(or_1_out), .Q(M5), .reset(Reset));  // open: Qn, preset, en
  or or_1 (or_1_out, demultiplexer_1_out1, LeerNuevaLinea, demultiplexer_2_out0);
  or or_2 (Escribir_RAM, M2, M4);
  or or_3 (RAM_Control, M1, M2, M3, M4, M5);
  or or_4 (Load_Register_File, LSP2, ALU_Tip_R_and_Tip_I, Mov_Operation, R_W_RF2, EN_RND, KBD);
  Demultiplexer #(.enable("false")) demultiplexer_2 (.out0(demultiplexer_2_out0), .out1(LI1), .in(M5), .sel(Wait));
  D_Flip_Flop d_ff_2 (.clk(Reloj), .D(LSP1), .Q(LM5), .reset(Reset));  // open: Qn, preset, en
  or or_5 (or_5_out, LI1, Camb_Instr);
  D_Flip_Flop d_ff_3 (.clk(Reloj), .D(or_5_out), .Q(d_ff_3_q), .reset(Reset));  // open: Qn, preset, en
  Demultiplexer #(.select(4), .enable("false")) demultiplexer_3 (
    .out0(Jmp_nop_Jr), .out1(ALU_Tip_R_and_Tip_I), .out2(Mov_Operation), .out3(Halt), .out4(TTY_ENABLE),
    .out5(EN_RND), .out6(LM4), .out7(LSP1), .out8(LM3), .out9(LM2), .out10(KBD), .in(d_ff_3_q),
    .sel(operacion));  // open: out11, out12, out13, out14, out15
  D_Flip_Flop d_ff_4 (.clk(Reloj), .D(LM5), .Q(d_ff_4_q), .reset(Reset));  // open: Qn, preset, en
  D_Flip_Flop d_ff_5 (.clk(Reloj), .D(LM2), .Q(d_ff_5_q), .reset(Reset));  // open: Qn, preset, en
  D_Flip_Flop d_ff_6 (.clk(Reloj), .D(LM4), .Q(d_ff_6_q), .reset(Reset));  // open: Qn, preset, en
  D_Flip_Flop d_ff_7 (.clk(Reloj), .D(LM3), .Q(d_ff_7_q), .reset(Reset));  // open: Qn, preset, en
  or or_6 (or_6_out, demultiplexer_4_out0, d_ff_6_q);
  or or_7 (or_7_out, demultiplexer_5_out0, d_ff_7_q);
  or or_8 (or_8_out, demultiplexer_6_out0, d_ff_5_q);
  D_Flip_Flop d_ff_8 (.clk(Reloj), .D(or_6_out), .Q(M3), .reset(Reset));  // open: Qn, preset, en
  or or_9 (or_9_out, d_ff_4_q, demultiplexer_7_out0);
  D_Flip_Flop d_ff_9 (.clk(Reloj), .D(or_7_out), .Q(M1), .reset(Reset));  // open: Qn, preset, en
  D_Flip_Flop d_ff_10 (.clk(Reloj), .D(or_8_out), .Q(M2), .reset(Reset));  // open: Qn, preset, en
  Demultiplexer #(.enable("false")) demultiplexer_4 (.out0(demultiplexer_4_out0), .out1(LSP2), .in(M3), .sel(Wait));
  D_Flip_Flop d_ff_11 (.clk(Reloj), .D(or_9_out), .Q(M4), .reset(Reset));  // open: Qn, preset, en
  Demultiplexer #(.enable("false")) demultiplexer_5 (.out0(demultiplexer_5_out0), .out1(R_W_RF2), .in(M1), .sel(Wait));
  Demultiplexer #(.enable("false")) demultiplexer_6 (
    .out0(demultiplexer_6_out0), .out1(demultiplexer_6_out1), .in(M2), .sel(Wait));
  Demultiplexer #(.enable("false")) demultiplexer_7 (
    .out0(demultiplexer_7_out0), .out1(demultiplexer_7_out1), .in(M4), .sel(Wait));
  D_Flip_Flop d_ff_12 (.clk(Reloj), .D(TTY_ENABLE), .Q(d_ff_12_q), .reset(Reset));  // open: Qn, preset, en
  D_Flip_Flop GUARDAR_DATO (.clk(Reloj), .D(R_W_RF2), .Q(GUARDAR_DATO_q), .reset(Reset));  // open: Qn, preset, en
  D_Flip_Flop GUARDAR_DATO_2 (.clk(Reloj), .D(LSP2), .Q(GUARDAR_DATO_2_q), .reset(Reset));  // open: Qn, preset, en
  D_Flip_Flop d_ff_13 (.clk(Reloj), .D(demultiplexer_7_out1), .Q(d_ff_13_q));  // open: Qn, preset, en, reset
  D_Flip_Flop d_ff_14 (.clk(Reloj), .D(KBD), .Q(KBD_ENABLE), .reset(Reset));  // open: Qn, preset, en
  or or_10 (out_15, GUARDAR_DATO_q, demultiplexer_6_out1, GUARDAR_DATO_2_q, d_ff_13_q);
  D_Flip_Flop d_ff_15 (.clk(Reloj), .D(out_15), .Q(d_ff_15_q), .reset(Reset));  // open: Qn, preset, en
  Demultiplexer #(.enable("false")) demultiplexer_8 (
    .out0(demultiplexer_8_out0), .out1(demultiplexer_8_out1), .in(d_ff_15_q), .sel(in_5));
  D_Flip_Flop d_ff_16 (.clk(Reloj), .D(demultiplexer_8_out1), .Q(d_ff_16_q), .reset(Reset));  // open: Qn, preset, en
  or or_11 (Load_Program_Counter, Jmp_nop_Jr, ALU_Tip_R_and_Tip_I, Mov_Operation, demultiplexer_8_out0, d_ff_16_q, EN_RND, KBD_ENABLE, d_ff_12_q);
  or or_12 (LOADSP, LSP1, LSP2);
  D_Flip_Flop esperar_actualizacionPC (
    .clk(Reloj), .D(Load_Program_Counter), .Q(LM1), .reset(Reset));  // open: Qn, preset, en
  or or_13 (out_16, LI, LI1);
  D_Flip_Flop cambio_de_linea (
    .clk(Reloj), .D(in_5), .Q(cambio_de_linea_q), .reset(or_14_out));  // open: Qn, preset, en
  or or_14 (or_14_out, Reset, out_15);
  D_Flip_Flop guardar_adress (.clk(Reloj), .D(LM1), .Q(LI), .reset(Reset));  // open: Qn, preset, en
  D_Flip_Flop d_ff_17 (.clk(Reloj), .D(LI), .Q(d_ff_17_q), .reset(Reset));  // open: Qn, preset, en
  D_Flip_Flop cambio_de_linea_2 (
    .clk(Reloj), .D(cambio_de_linea_q), .Q(cambio_de_linea_2_q), .reset(or_15_out));  // open: Qn, preset, en
  or or_15 (or_15_out, Reset, out_15);
  Demultiplexer #(.enable("false")) demultiplexer_9 (
    .out0(Camb_Instr), .out1(LeerNuevaLinea), .in(d_ff_17_q), .sel(cambio_de_linea_2_q));
  or or_16 (or_16_out, \end , Halt);
  or or_17 (LoadMemory, LM1, LM2, LM3, LM4, LM5, out_15);
  D_Flip_Flop u_END (.clk(Reloj), .D(or_16_out), .Q(\end ), .reset(Reset));  // open: Qn, preset, en

  // Other names for the same wires on the sheet: CargarNuevaLinea = in_5; CLK = Reloj; CS = RAM_Control;
  //   E_KBD = KBD_ENABLE; Load = LM3; Load_PC = Load_Program_Counter; Op[3:0] = operacion; Pop = LM4; Push = LSP1;
  //   R_W_Cach = Escribir_RAM; R_W_Cach_0 = M2; R_W_Cach_1 = M4; R_W_RF = Load_Register_File;
  //   R_W_RF0 = ALU_Tip_R_and_Tip_I; R_W_RF1 = Mov_Operation; R_W_RF3 = LSP2; R_W_RF6 = KBD; R_W_RF5 = EN_RND;
  //   Random = EN_RND; Resert = Reset; LM6 = out_15; RO = out_15; Store = LM2; TTY = TTY_ENABLE; TTYEN = TTY_ENABLE

  // Notes on the sheet:
  //   cargar nueva linea
  //   Entradas
  //   Selector de Operacion
  //   INDLE
  //   Control Unit
  //   Activa si se va a escribir en la RAM
  //   Cargar info de la RAM
  //   Activar el load de los registros
  //   ACTUALIZAR DIRECCION   NECESITA 
  //   Activa el Ram Control
  //   ACTUALIZAR DIRECCION   NECESITA 
  //   ACTUALIZAR DIRECCION   NECESITA 
  //   ACTUALIZAR DIRECCION   NECESITA 
  //   Jmp, nor, Jr
  //   Alu (Tipo R and Tipo I)
  //   Mover los registros
  //   Operaciones
  //   Instrucciones de Memoria
  //   un tiempo para la correcta actualizacion del cmabio de linea 
  //   para la buena actualizacion del cambio de linea 
  //   Cambio de instruccion
  //   OUTPUT DATA
  //   RESETEA A LA DIRECCION ANTIGUA 
endmodule
