// Logisim project Register File.circ as structural Verilog: 1 circuit, main circuit Register File
module Register_File (
  input  Reloj,
  input  Reset,
  input  RW,
  input  [31:0] DI,
  input  [4:0] DA,
  input  [4:0] SA,
  input  [4:0] SB,
  input  Mult_or_Div,
  input  [31:0] HI,
  input  [31:0] Lo,
  output [31:0] Output_Hi,
  output [31:0] Output_Lo,
  output [31:0] Output_A,
  output [31:0] Output__B
);

  wire D1, D2, D3, D4, D5, D6, D7, D8, D9, D10, D11, D12, D13, D14, D15, D16, D17, D18, D19, D20, D21, D22,
       D23, D24, D25, D26, D27, D28, D29, D30;
  wire [31:0] Out1, Out2, Out3, Out4, Out5, Out6, Out7, Out8, Out9, Out10, Out11, Out12, Out13, Out14, Out15,
       Out16, Out17, Out18, Out19, Out20, Out21, Out22, Out23, Out24, Out25, Out26, Out27, Out28, Out29,
       Out30, SP, SP_4, SP_4_t;

  Register #(.width(32)) R1 (.D(DI), .en(D1), .Q(Out1), .clk(Reloj), .clr(Reset));
  Register #(.width(32)) R2 (.D(DI), .en(D2), .Q(Out2), .clk(Reloj), .clr(Reset));
  Register #(.width(32)) R3 (.D(DI), .en(D3), .Q(Out3), .clk(Reloj), .clr(Reset));
  Register #(.width(32)) R4 (.D(DI), .en(D4), .Q(Out4), .clk(Reloj), .clr(Reset));
  Decoder #(.select(5), .disabled(0)) decoder_1 (
    .out1(D1), .out2(D2), .out3(D3), .out4(D4), .out5(D5), .out6(D6), .out7(D7), .out8(D8), .out9(D9),
    .out10(D10), .out11(D11), .out12(D12), .out13(D13), .out14(D14), .out15(D15), .out16(D16), .out17(D17),
    .out18(D18), .out19(D19), .out20(D20), .out21(D21), .out22(D22), .out23(D23), .out24(D24), .out25(D25),
    .out26(D26), .out27(D27), .out28(D28), .out29(D29), .out30(D30), .out31(D30), .sel(DA), .en(RW));  // open: out0
  Register #(.width(32)) R5 (.D(DI), .en(D5), .Q(Out5), .clk(Reloj), .clr(Reset));
  Register #(.width(32)) R6 (.D(DI), .en(D6), .Q(Out6), .clk(Reloj), .clr(Reset));
  Register #(.width(32)) R7 (.D(DI), .en(D7), .Q(Out7), .clk(Reloj), .clr(Reset));
  Register #(.width(32)) R8 (.D(DI), .en(D8), .Q(Out8), .clk(Reloj), .clr(Reset));
  Register #(.width(32)) R9 (.D(DI), .en(D9), .Q(Out9), .clk(Reloj), .clr(Reset));
  Register #(.width(32)) R10 (.D(DI), .en(D10), .Q(Out10), .clk(Reloj), .clr(Reset));
  Register #(.width(32)) R11 (.D(DI), .en(D11), .Q(Out11), .clk(Reloj), .clr(Reset));
  Register #(.width(32)) R12 (.D(DI), .en(D12), .Q(Out12), .clk(Reloj), .clr(Reset));
  Register #(.width(32)) R13 (.D(DI), .en(D13), .Q(Out13), .clk(Reloj), .clr(Reset));
  Register #(.width(32)) R14 (.D(DI), .en(D14), .Q(Out14), .clk(Reloj), .clr(Reset));
  Register #(.width(32)) R15 (.D(DI), .en(D15), .Q(Out15), .clk(Reloj), .clr(Reset));
  Register #(.width(32)) R16 (.D(DI), .en(D16), .Q(Out16), .clk(Reloj), .clr(Reset));
  Multiplexer #(.select(5), .width(32), .enable("false")) multiplexer_1 (
    .in0({32{1'b0}}), .in1(Out1), .in2(Out2), .in3(Out3), .in4(Out4), .in5(Out5), .in6(Out6), .in7(Out7),
    .in8(Out8), .in9(Out9), .in10(Out10), .in11(Out11), .in12(Out12), .in13(Out13), .in14(Out14),
    .in15(Out15), .in16(Out16), .in17(Out17), .in18(Out18), .in19(Out19), .in20(Out20), .in21(Out21),
    .in22(Out22), .in23(Out23), .in24(Out24), .in25(Out25), .in26(Out26), .in27(Out27), .in28(Out28),
    .in29(Out29), .in30(Out30), .in31(SP), .out(Output_A), .sel(SA));
  Register #(.width(32)) R17 (.D(DI), .en(D17), .Q(Out17), .clk(Reloj), .clr(Reset));
  Register #(.width(32)) R18 (.D(DI), .en(D18), .Q(Out18), .clk(Reloj), .clr(Reset));
  Register #(.width(32)) R19 (.D(DI), .en(D19), .Q(Out19), .clk(Reloj), .clr(Reset));
  Register #(.width(32)) R20 (.D(DI), .en(D20), .Q(Out20), .clk(Reloj), .clr(Reset));
  Register #(.width(32)) R21 (.D(DI), .en(D21), .Q(Out21), .clk(Reloj), .clr(Reset));
  Register #(.width(32)) R22 (.D(DI), .en(D22), .Q(Out22), .clk(Reloj), .clr(Reset));
  Register #(.width(32)) R23 (.D(DI), .en(D23), .Q(Out23), .clk(Reloj), .clr(Reset));
  Register #(.width(32)) R24 (.D(DI), .en(D24), .Q(Out24), .clk(Reloj), .clr(Reset));
  Multiplexer #(.select(5), .width(32), .enable("false")) multiplexer_2 (
    .in0({32{1'b0}}), .in1(Out1), .in2(Out2), .in3(Out3), .in4(Out4), .in5(Out5), .in6(Out6), .in7(Out7),
    .in8(Out8), .in9(Out9), .in10(Out10), .in11(Out11), .in12(Out12), .in13(Out13), .in14(Out14),
    .in15(Out15), .in16(Out16), .in17(Out17), .in18(Out18), .in19(Out19), .in20(Out20), .in21(Out21),
    .in22(Out22), .in23(Out23), .in24(Out24), .in25(Out25), .in26(Out26), .in27(Out27), .in28(Out28),
    .in29(Out29), .in30(Out30), .in31(SP), .out(Output__B), .sel(SB));
  Register #(.width(32)) R25 (.D(DI), .en(D25), .Q(Out25), .clk(Reloj), .clr(Reset));
  Register #(.width(32)) R26 (.D(DI), .en(D26), .Q(Out26), .clk(Reloj), .clr(Reset));
  Register #(.width(32)) R27 (.D(DI), .en(D27), .Q(Out27), .clk(Reloj), .clr(Reset));
  Register #(.width(32)) R28 (.D(DI), .en(D28), .Q(Out28), .clk(Reloj), .clr(Reset));
  Register #(.width(32)) R29 (.D(DI), .en(D29), .Q(Out29), .clk(Reloj), .clr(Reset));
  Register #(.width(32)) R30 (.D(DI), .en(D30), .Q(Out30), .clk(Reloj), .clr(Reset));
  Adder #(.width(32)) adder_1 (.a(SP), .b(32'h4), .out(SP_4));  // open: cin, cout
  Subtractor #(.width(32)) subtractor_1 (.a(SP), .b(32'h4), .out(SP_4_t));  // open: bin, bout
  Register #(.width(32)) u_Hi (.D(HI), .en(Mult_or_Div), .Q(Output_Hi), .clk(Reloj), .clr(Reset));
  Register #(.width(32)) u_Lo (.D(Lo), .en(Mult_or_Div), .Q(Output_Lo), .clk(Reloj), .clr(Reset));
  // Probe on Output_A
  // Probe on Output__B

  // Other names for the same wires on the sheet: CLK = Reloj; Input[31:0] = DI; Registro_A[31:0] = Output_A;
  //   Registro_B[31:0] = Output__B; Write_Hi_Lo = Mult_or_Div

  // Notes on the sheet:
  //   Reset
  //   RW
  //   Dato de Entrada
  //   SELECTORES
  //   Data Address
  //   SA
  //   SB
  //   INPUTS
  //   Ro
  //   Read Or Write
  //   SELECTORES
  //   Selector de Registro A
  //   REGISTROS
  //   Selector de Registro B
  //   Stack Pointer
  //   R31
  //   OUTPUTS
endmodule
